# Fritzing sketch turntable (saved by Fritzing 0.9.2b)
breadboards: 1

parts:
  M1 = DC Motor
  D1 = Zener Diode [part_number=1N4732A breakdown_voltage=3.6V package="300 mil [THT]"]
  R1 = Resistor [tolerance=±5% resistance=1k package=THT]
  Q1 = NPN-Transistor [package="SOT-23 [SMD]"]
  Part1 = Arduino Leonardo (Rev3b)
  J6 = Power Jack [package=power_jack_smd]
  R2 = Rotary Potentiometer (Small) [maximum_resistance=100kΩ package=THT]
  R3 = Resistor [tolerance=±5% resistance=100 package=THT]
  R4 = Resistor [tolerance=±5% resistance=160 package=THT]
  R5 = Resistor [tolerance=±5% resistance=220 package=THT]
  R6 = Resistor [tolerance=±5% resistance=330 package=THT]
  R7 = Resistor [tolerance=±5% resistance=680 package=THT]
  R8 = Resistor [tolerance=±5% resistance=470 package=THT]
  R9 = Resistor [tolerance=±5% resistance=1k package=THT]
  S1 = Square Pushbutton
  S2 = Square Pushbutton
  S3 = Square Pushbutton
  S4 = Square Pushbutton
  S5 = Square Pushbutton
  S6 = Square Pushbutton
  R10 = Rotary Potentiometer (Small) [maximum_resistance=100kΩ package=THT]
  Q2 = LTR-301 [package=ltr-301]
  LED2 = smd LED [color="Infrared (850nm)" package="0603 [SMD]"]
  R11 = Resistor [tolerance=±5% resistance=1M package=THT]
  R12 = Resistor [tolerance=±5% resistance=270 package=THT]

nets:
  N1: M1.pin_1, D1.cathode
  N2: M1.pin_2, J6.PWR
  N3: D1.anode, Q1.1
  N4: R1.Pin_0, Q1.0
  GND: Q1.2, Part1.GND, J6.GND, R2.leg1, R2.leg2, R3.Pin_1, R4.Pin_1, R5.Pin_1, R6.Pin_1, R7.Pin_1, R8.Pin_1, R9.Pin_1, R10.leg1, Q2.E, LED2.cathode
  N5: Part1.D2/SDA, Part1.A1, R9.Pin_0, S1.leg0, S2.leg0, S3.leg0, S4.leg0, S5.leg0, S6.leg0, R10.leg2
  N6: Part1.5V, R11.Pin_0, R12.Pin_0
  N7: Part1.A0, R2.wiper
  N8: Part1.A2, Q2.C, R11.Pin_1
  N9: Part1.A3, R10.wiper
  N10: R3.Pin_0, S5.leg1
  N11: R4.Pin_0, S6.leg1
  N12: R5.Pin_0, S2.leg1
  N13: R6.Pin_0, S1.leg1
  N14: R7.Pin_0, S3.leg1
  N15: R8.Pin_0, S4.leg1
  N16: LED2.anode, R12.Pin_1
